# Fritzing sketch GasPump (saved by Fritzing 0.9.3b)
breadboards: 1

parts:
  Part1 = Arduino Uno (Rev3)
  Pilot_Gas_Button = Pushbutton [package="[THT]"]
  Intel_Gas_Button = Pushbutton [package="[THT]"]
  Gunner_Gas_Button = Pushbutton [package="[THT]"]
  J2 = screw terminal, 6 pins
  R1 = Resistor [tolerance=±5% resistance=560 package=THT]  # not connected
  R3 = Resistor [tolerance=±5% resistance=560 package=THT]  # not connected
  R4 = Resistor [tolerance=±5% resistance=560 package=THT]  # not connected
  Main_Tank = Neopixel Strip -- Black (30/m) [part_number=1376]
  Pilot_Tank = Neopixel Strip -- White (60/m) [part_number=1138]
  R5 = Resistor [tolerance=±5% resistance=560 package=THT]  # not connected
  Intel_Tank = Neopixel Strip -- White (60/m) [part_number=1138]
  Gun_Tank = Neopixel Strip -- White (60/m) [part_number=1138]
  J3 = screw terminal, 3 pins
  R6 = Resistor [tolerance=±5% resistance=560 package=THT]  # not connected
  J4 = screw terminal, 3 pins
  R7 = Resistor [tolerance=±5% resistance=560 package=THT]  # not connected
  J5 = screw terminal, 3 pins
  Gas_Nozzle_Button = Pushbutton [package="[THT]"]
  R8 = Resistor [tolerance=±5% resistance=220 package=THT]

nets:
  N1: Part1.D9_PWM, Gun_Tank.DI, J3.pin2
  N2: Part1.D2, J5.pin1, J5.pin2, Gas_Nozzle_Button.Pin_3, Gas_Nozzle_Button.Pin_4, R8.Pin_1
  +5V: Part1.5V, Pilot_Tank.+5V, Intel_Tank.+5V, J5.pin3, Gas_Nozzle_Button.Pin_1, Gas_Nozzle_Button.Pin_2
  GND: Part1.GND, Pilot_Tank.GND, Intel_Tank.GND, R8.Pin_0
  N3: Pilot_Gas_Button.Pin_1, J2.pin4
  N4: Pilot_Gas_Button.Pin_3, J2.pin3
  N5: Intel_Gas_Button.Pin_1, J2.pin2
  N6: Intel_Gas_Button.Pin_3, J2.pin1
  N7: Gunner_Gas_Button.Pin_1, J2.pin6
  N8: Gunner_Gas_Button.Pin_3, J2.pin5
  N9: Main_Tank.GND, J4.pin3
  N10: Main_Tank.Din, J4.pin2
  N11: Main_Tank.+5V, J4.pin1
  N12: Gun_Tank.+5V, J3.pin1
  N13: Gun_Tank.GND, J3.pin3

notes:
  Thinking of making the Main tank with 10 lights be put on its own power source

custom parts:
  Neopixel Strip -- Black (30/m): These NeoPixel strips have 30 digitally-addressable pixel LEDs per meter and are very affordable and are only 12.5 mm wide, 10 mm if you remove the strip from the casing.
  Neopixel Strip -- White (60/m): Neopixel Strip, White, 60 pixels per meter.
