# Fritzing sketch consolePanel (saved by Fritzing 0.9.3b)
breadboards: 1

parts:
  Part1 = Arduino Uno (Rev3)
  R2 = Resistor [tolerance=±5% resistance=220 package=THT]
  R3 = Resistor [tolerance=±5% resistance=560 package=THT]
  R4 = Resistor [tolerance=±5% resistance=560 package=THT]
  R5 = Resistor [tolerance=±5% resistance=220 package=THT]
  R6 = Resistor [tolerance=±5% resistance=560 package=THT]
  R7 = Resistor [tolerance=±5% resistance=220 package=THT]
  R8 = Resistor [tolerance=±5% resistance=560 package=THT]
  R9 = Resistor [tolerance=±5% resistance=560 package=THT]
  R10 = Resistor [tolerance=±5% resistance=220 package=THT]
  R11 = Resistor [tolerance=±5% resistance=220 package=THT]
  R12 = Resistor [tolerance=±5% resistance=220 package=THT]
  R13 = Resistor [tolerance=±5% resistance=220 package=THT]
  R14 = Resistor [tolerance=±5% resistance=220 package=THT]
  R15 = Resistor [tolerance=±5% resistance=220 package=THT]
  J1 = screw terminal, 3 pins
  J2 = screw terminal, 3 pins
  R16 = Resistor [tolerance=±5% resistance=220 package=THT]
  F1 = Waterproof Pushbutton (red)
  F2 = Waterproof Pushbutton (red)
  F3 = Waterproof Pushbutton (red)
  F4 = Waterproof Pushbutton (red)
  F5 = Waterproof Pushbutton (red)
  J3 = screw terminal, 3 pins
  J4 = screw terminal, 3 pins
  J5 = screw terminal, 3 pins
  J6 = screw terminal, 3 pins
  J7 = screw terminal, 3 pins
  J8 = screw terminal, 3 pins
  J9 = screw terminal, 3 pins
  J10 = screw terminal, 3 pins
  D1 = Rotary Potentiometer (Small) [maximum_resistance=100kΩ package=THT]
  D2 = Rotary Potentiometer (Small) [maximum_resistance=100kΩ package=THT]
  D3 = Rotary Potentiometer (Small) [maximum_resistance=100kΩ package=THT]
  G1 = Toggle Switch [package=THT]
  G3 = Toggle Switch [package=THT]
  G4 = Toggle Switch [package=THT]
  G2 = Toggle Switch [package=THT]
  G5 = Toggle Switch [package=THT]
  J12 = screw terminal, 2 pins
  J13 = screw terminal, 2 pins
  J14 = screw terminal, 2 pins
  J15 = screw terminal, 2 pins
  J16 = screw terminal, 2 pins
  E1 = Rotary Potentiometer (Small) [maximum_resistance=100kΩ package=THT]
  E2 = Rotary Potentiometer (Small) [maximum_resistance=100kΩ package=THT]
  E3 = Rotary Potentiometer (Small) [maximum_resistance=100kΩ package=THT]
  J17 = screw terminal, 3 pins
  J18 = screw terminal, 3 pins
  J19 = screw terminal, 3 pins

nets:
  N1: Part1.A0, J10.pin2, D1.wiper
  N2: Part1.A1, J9.pin2, D2.wiper
  N3: Part1.A2, J8.pin2, D3.wiper
  N4: Part1.A3, E1.wiper, J17.pin2
  N5: Part1.A4/SDA, E2.wiper, J18.pin2
  N6: Part1.A5/SCL, E3.wiper, J19.pin2
  N7: Part1.D8, G2.L1, J13.pin2
  N8: Part1.D9_PWM, G3.L1, J14.pin2
  N9: Part1.D10_PWM/SS, G4.L1, J15.pin2
  N10: Part1.D11_PWM/MOSI, G5.L1, J16.pin2
  N11: Part1.D2, J2.pin1, R16.Pin_1, F1.no_name_yet#2
  N12: Part1.D3_PWM, R5.Pin_1, F2.no_name_yet#2, J3.pin2
  N13: Part1.D4, R7.Pin_1, F3.no_name_yet#2, J4.pin3
  N14: Part1.D5_PWM, R10.Pin_1, F4.no_name_yet#2, J6.pin1
  N15: Part1.D6_PWM, R2.Pin_1, F5.no_name_yet#2, J7.pin2
  N16: Part1.D7, G1.L1, J12.pin2
  N17: Part1.5V, R3.Pin_0, R4.Pin_0, R6.Pin_0, R8.Pin_0, R9.Pin_0, R10.Pin_0, J1.pin3, F1.no_name_yet#1, F2.no_name_yet#1, F3.no_name_yet#1, F4.no_name_yet#1, F5.no_name_yet#1, J3.pin1, J4.pin2, J5.pin3, J7.pin1, J8.pin1, J9.pin1, J10.pin1, D1.leg2, D2.leg2, D3.leg2, G1.COM, G3.COM, G5.COM, J12.pin1, J14.pin1, J16.pin1, E1.leg2, E2.leg2, E3.leg2, J17.pin1, J18.pin1, J19.pin1
  N18: Part1.GND, R2.Pin_0, R5.Pin_0, R7.Pin_0, R11.Pin_1, R12.Pin_1, R13.Pin_1, R14.Pin_1, R15.Pin_1, J1.pin2, J2.pin3, R16.Pin_0, F1.no_name_yet#5, F2.no_name_yet#5, F3.no_name_yet#5, F4.no_name_yet#5, F5.no_name_yet#5, J4.pin1, J5.pin2, J6.pin3, J8.pin3, J9.pin3, J10.pin3, D1.leg1, D2.leg1, D3.leg1, E1.leg1, E2.leg1, E3.leg1, J17.pin3, J18.pin3, J19.pin3
  N19: R3.Pin_1, J1.pin1, F1.no_name_yet#3, F1.no_name_yet#4
  N20: R4.Pin_1, F5.no_name_yet#4, J6.pin2
  N21: R6.Pin_1, J2.pin2, F2.no_name_yet#4
  N22: R8.Pin_1, F3.no_name_yet#4, J3.pin3
  N23: R9.Pin_1, F4.no_name_yet#4, J5.pin1
  N24: R11.Pin_0, G4.COM, J15.pin1
  N25: R12.Pin_0, G2.COM, J13.pin1

custom parts:
  Waterproof Pushbutton (red): Waterproof Illuminated Pushbutton (red)
