# Fritzing sketch gunnar (saved by Fritzing 0.9.3b)
breadboards: 1

parts:
  Part1 = Arduino Leonardo (Rev3b)
  R1 = Resistor [tolerance=±5% resistance=220 package=THT]
  J1 = screw terminal, 3 pins
  '2'_Key = Pushbutton [package="[THT]"]
  '1'_Key = Pushbutton [package="[THT]"]
  '3'_Key = Pushbutton [package="[THT]"]
  J2 = screw terminal, 3 pins
  R2 = Resistor [tolerance=±5% resistance=220 package=THT]
  J3 = screw terminal, 3 pins
  R3 = Resistor [tolerance=±5% resistance=220 package=THT]
  R4 = Resistor [tolerance=±5% resistance=10k package=THT]
  R6 = Resistor [tolerance=±5% resistance=220 package=THT]
  R7 = Resistor [tolerance=±5% resistance=220 package=THT]
  LED1 = LED - 5mm [color="Red (633nm)" package="5 mm [THT]"]
  LED2 = LED - 5mm [color="Green (555nm)" package="5 mm [THT]"]
  LED3 = LED - 5mm [color="Blue (525nm)" package="5 mm [THT]"]
  J6 = screw terminal, 3 pins
  J7 = screw terminal, 3 pins
  J8 = screw terminal, 3 pins
  U1 = SLIDER [package=slider]
  R8 = Resistor [tolerance=±5% resistance=100 package=THT]

nets:
  N1: Part1.D2/SDA, R1.Pin_0, J1.pin2, J1.pin3, '2'_Key.Pin_1, '2'_Key.Pin_2
  N2: Part1.D3_PWM/SCL, Part1.SCL, '3'_Key.Pin_1, '3'_Key.Pin_2, J3.pin2, J3.pin3, R3.Pin_0
  N3: Part1.D4/A6, '1'_Key.Pin_1, '1'_Key.Pin_2, J2.pin2, J2.pin3, R2.Pin_0
  N4: Part1.5V, J1.pin1, '2'_Key.Pin_3, '2'_Key.Pin_4, '1'_Key.Pin_3, '3'_Key.Pin_3, J2.pin1, J3.pin1
  N5: Part1.GND, R1.Pin_1, R2.Pin_1, R3.Pin_1, R4.Pin_0, R6.Pin_0, R7.Pin_0, R8.Pin_0
  N6: Part1.A0, J8.pin2, U1.A
  N7: Part1.D10_PWM/A10, LED3.anode, J7.pin2
  N8: Part1.D11_PWM, LED2.anode, J6.pin1
  N9: Part1.D12/A11, LED1.anode, J6.pin3
  N10: R4.Pin_1, LED3.cathode, J7.pin3
  N11: R6.Pin_1, LED1.cathode, J7.pin1
  N12: R7.Pin_1, LED2.cathode, J6.pin2
  N13: J8.pin1, U1.S
  N14: J8.pin3, U1.E, R8.Pin_1
