# Fritzing sketch illuminatedPushbuttonWiring (saved by Fritzing 0.9.3b)
breadboards: 1

parts:
  R1 = Resistor [tolerance=±5% resistance=220 package=THT]
  J1 = Screw terminal - 2 pins [package=THT]
  Part1 = Arduino Uno (Rev3)
  Illuminated_Push = Waterproof Pushbutton (red)
  R2 = Resistor [tolerance=±5% resistance=560 package=THT]  # not connected

nets:
  N1: R1.Pin_0, Part1.D2, Illuminated_Push.no_name_yet#2
  N2: R1.Pin_1, J1.pin2, Illuminated_Push.no_name_yet#5
  N3: J1.pin1, Illuminated_Push.no_name_yet#4

notes:
  As they don't have exactly the illuminated push So I improvised. Ignore NC

custom parts:
  Waterproof Pushbutton (red): Waterproof Illuminated Pushbutton (red)
